// Logisim project pipelined.circ as structural Verilog: 11 circuits, main circuit main
module ALU_control (
  input  [1:0] ALUop,
  input  [5:0] Funct,
  input  [2:0] IMM_OP,
  output [3:0] Output
);

  // PLA #(.in_width(11), .out_width(4), .truth_table("00xxxxxxxxx,0010#lw/sw\n01xxxxxxxxx,0110#beq/bne\n10xxx100001,0010#addu\n10xxx100011,0110#subu\n10xxx100100,0000#AND\n10xxx100101,0001#OR\n10xxx100111,1100#nor\n10xxx101010,0111#slt\n11001xxxxxx,0010#addiu\n11010xxxxxx,0111#slti\n11100xxxxxx,0000#andi\n11101xxxxxx,0001#ori\n10xxx000010,0010#jr\n10xxx000011,0010#jral")) pla_1: pin names not known; wires that end beside it: Output
endmodule

module Bit_extender (
  input  [15:0] Input,
  input  Signed,
  output [31:0] Output
);

  wire and_1_out;

  Multiplexer #(.width(16)) multiplexer_1 (.in0({16{1'b0}}), .in1({16{1'b1}}), .out(Output[31:16]), .sel(and_1_out));
  and and_1 (and_1_out, Input[15], Signed);

  assign Output[15:0] = Input;
endmodule

module main (
);

  wire and_1_out, control_1_signedimm, ex_mem_1_registerwrite_2, ex_mem_1_zero_2, mips_alu_1_p4,
       mipsprogramrom_1_p3, or_1_out, registerfile_1_p2, xor_1_out;
  wire [0:0] id_ex_1_alu_2;
  wire [1:0] control_1_memory, control_1_registerwrite, control_1_registerwritesrc, ex_mem_1_memory_2,
       ex_mem_1_registerwritesrc_2, id_ex_1_alu_2_2, id_ex_1_memory_2, id_ex_1_registerwrite_2,
       id_ex_1_registerwritesrc_2, mem_wb_1_registerwritesrc_2;
  wire [2:0] control_1_alu, control_1_branching, ex_mem_1_branch_2, id_ex_1_branch_2, id_ex_1_op_2;
  wire [3:0] mips_alu_1_p3;
  wire [4:0] ex_mem_1_regdst_2, id_ex_1_op_2_4, id_ex_1_op_2_5, id_ex_1_registerrs_2, id_ex_1_registerrt_2,
       multiplexer_5_out, registerfile_1_p3;
  wire [23:0] ex_mem_1_aluresult_2;
  wire [27:2] id_ex_1_op_2_3;
  wire [31:0] adder_1_out, adder_2_out, bit_extender_1_output, ex_mem_1_branchpc_2, ex_mem_1_jalpc_2,
       ex_mem_1_jumppc_2, ex_mem_1_writedata_2, id_ex_1_data1_2, id_ex_1_data2_2, id_ex_1_imm_2,
       id_ex_1_pc_2, if_id_1_op_2, if_id_1_pc_2, mem_wb_1_aluresult_2, mem_wb_1_jalpc_2,
       mem_wb_1_memoryresult_2, mips_alu_1_p2, mips_alu_1_p5, mips_ram_1_p6, mipsprogramrom_1_p2,
       multiplexer_1_out, multiplexer_2_out, multiplexer_3_out, multiplexer_6_out, PC_q, registerfile_1_p1,
       registerfile_1_p6, registerfile_1_p7, shifter_1_out;
  wire [31:24] ex_mem_1_aluresult_2_2;
  wire [31:29] id_ex_1_op_2_2;

  Register #(.width(32)) PC (.D(multiplexer_1_out), .en(1'b1), .Q(PC_q), .clk(mipsprogramrom_1_p3));  // open: clr
  Multiplexer #(.width(32)) multiplexer_1 (
    .in0(adder_1_out), .in1(multiplexer_6_out), .out(multiplexer_1_out), .sel(and_1_out));
  Adder #(.width(32)) adder_1 (.a(32'h4), .b(PC_q), .out(adder_1_out));  // open: cin, cout
  // MIPSProgramROM mipsprogramrom_1: pin names not known; wires that end beside it: PC_q, mipsprogramrom_1_p2, mipsprogramrom_1_p3
  IF_ID if_id_1 (
    .PC(adder_1_out), .OP(mipsprogramrom_1_p2), .Clear(and_1_out), .Stall(1'b0), .Clock(mipsprogramrom_1_p3),
    .PC_2(if_id_1_pc_2), .OP_2(if_id_1_op_2));
  Clock clock_1 (.out(mipsprogramrom_1_p3));
  // RegisterFile #(.trigger("falling")) registerfile_1: pin names not known; wires that end beside it: registerfile_1_p1, registerfile_1_p2, registerfile_1_p3, if_id_1_op_2[25:21], if_id_1_op_2[20:16], registerfile_1_p6, registerfile_1_p7
  Bit_extender bit_extender_1 (
    .Input(if_id_1_op_2[15:0]), .Signed(control_1_signedimm), .Output(bit_extender_1_output));
  Control control_1 (
    .Funct(if_id_1_op_2[5:0]), .OP(if_id_1_op_2[31:26]), .SignedIMM(control_1_signedimm),
    .Alu(control_1_alu), .Branching(control_1_branching), .Memory(control_1_memory),
    .RegisterWriteSrc(control_1_registerwritesrc), .RegisterWrite(control_1_registerwrite));
  ID_EX id_ex_1 (
    .Data1(registerfile_1_p6), .Data2(registerfile_1_p7), .RegisterRt(if_id_1_op_2[25:21]),
    .RegisterRs(if_id_1_op_2[20:16]), .IMM(bit_extender_1_output), .PC(if_id_1_pc_2), .OP(if_id_1_op_2),
    .ALU(control_1_alu), .Branch(control_1_branching), .Memory(control_1_memory),
    .RegisterWriteSrc(control_1_registerwritesrc), .RegisterWrite(control_1_registerwrite),
    .Clear(and_1_out), .Stall(1'b0), .Clock(mipsprogramrom_1_p3), .Data1_2(id_ex_1_data1_2),
    .Data2_2(id_ex_1_data2_2), .RegisterRt_2(id_ex_1_registerrt_2), .RegisterRs_2(id_ex_1_registerrs_2),
    .IMM_2(id_ex_1_imm_2), .PC_2(id_ex_1_pc_2),
    .OP_2({id_ex_1_op_2_2, id_ex_1_op_2, id_ex_1_op_2_3[27:23], id_ex_1_op_2_5, id_ex_1_op_2_4, id_ex_1_op_2_3[12:2]}),
    .ALU_2({id_ex_1_alu_2_2, id_ex_1_alu_2[0]}), .Branch_2(id_ex_1_branch_2), .Memory_2(id_ex_1_memory_2),
    .RegisterWriteSrc_2(id_ex_1_registerwritesrc_2), .RegisterWrite_2(id_ex_1_registerwrite_2));
  Multiplexer #(.select(2), .width(32)) multiplexer_2 (
    .in0(id_ex_1_data2_2), .in1(registerfile_1_p1), .in2({ex_mem_1_aluresult_2_2, ex_mem_1_aluresult_2}),
    .out(multiplexer_2_out), .sel(2'b00));  // open: in3
  Multiplexer #(.select(2), .width(32)) multiplexer_3 (
    .in0(id_ex_1_data1_2), .in1(registerfile_1_p1), .in2({ex_mem_1_aluresult_2_2, ex_mem_1_aluresult_2}),
    .out(multiplexer_3_out), .sel(2'b00));  // open: in3
  // Mips_ALU mips_alu_1: pin names not known; wires that end beside it: multiplexer_3_out, mips_alu_1_p2, mips_alu_1_p3, mips_alu_1_p4, mips_alu_1_p5
  Multiplexer #(.width(32)) multiplexer_4 (
    .in0(id_ex_1_imm_2), .in1(multiplexer_2_out), .out(mips_alu_1_p2), .sel(id_ex_1_alu_2[0]));
  ALU_Control_2 alu_control_2_1 (
    .Output(mips_alu_1_p3), .ALUop(id_ex_1_alu_2_2), .Funct(id_ex_1_op_2_3[7:2]), .IMM_OP(id_ex_1_op_2));
  Shifter #(.width(32)) shifter_1 (.in(id_ex_1_imm_2), .\dist (5'b00010), .out(shifter_1_out));
  Adder #(.width(32)) adder_2 (.a(shifter_1_out), .b(id_ex_1_pc_2), .out(adder_2_out));  // open: cin, cout
  Multiplexer #(.width(5)) multiplexer_5 (
    .in0(id_ex_1_op_2_5), .in1(id_ex_1_op_2_4), .out(multiplexer_5_out), .sel(id_ex_1_registerwrite_2[0]));
  EX_MEM ex_mem_1 (
    .Zero(mips_alu_1_p4), .AluResult(mips_alu_1_p5), .WriteData(multiplexer_2_out), .BranchPC(adder_2_out),
    .JumpPC({id_ex_1_pc_2[31:28], id_ex_1_op_2_3[27:23], id_ex_1_op_2_5, id_ex_1_op_2_4, id_ex_1_op_2_3[12:2], 2'b00}),
    .jalPC(id_ex_1_pc_2), .RegDst(multiplexer_5_out), .Branch(id_ex_1_branch_2), .Memory(id_ex_1_memory_2),
    .RegisterWriteSrc(id_ex_1_registerwritesrc_2), .RegisterWrite(id_ex_1_registerwrite_2[1]),
    .Clear(and_1_out), .Stall(1'b0), .Clock(mipsprogramrom_1_p3), .Zero_2(ex_mem_1_zero_2),
    .AluResult_2({ex_mem_1_aluresult_2_2, ex_mem_1_aluresult_2}), .WriteData_2(ex_mem_1_writedata_2),
    .BranchPC_2(ex_mem_1_branchpc_2), .JumpPC_2(ex_mem_1_jumppc_2), .jalPC_2(ex_mem_1_jalpc_2),
    .RegDst_2(ex_mem_1_regdst_2), .Branch_2(ex_mem_1_branch_2), .Memory_2(ex_mem_1_memory_2),
    .RegisterWriteSrc_2(ex_mem_1_registerwritesrc_2), .RegisterWrite_2(ex_mem_1_registerwrite_2));
  and and_1 (and_1_out, or_1_out, ex_mem_1_branch_2[2]);
  or or_1 (or_1_out, xor_1_out, ex_mem_1_branch_2[1]);
  xor xor_1 (xor_1_out, ex_mem_1_zero_2, ex_mem_1_branch_2[0]);
  Multiplexer #(.select(2), .width(32)) multiplexer_6 (
    .in0(ex_mem_1_branchpc_2), .in1(ex_mem_1_branchpc_2), .in2(ex_mem_1_jumppc_2),
    .in3({ex_mem_1_aluresult_2_2, ex_mem_1_aluresult_2}), .out(multiplexer_6_out),
    .sel(ex_mem_1_branch_2[1:0]));
  // MIPS_RAM #(.addrWidth(24)) mips_ram_1: pin names not known; wires that end beside it: ex_mem_1_aluresult_2, ex_mem_1_writedata_2, ex_mem_1_memory_2[1], ex_mem_1_memory_2[0], mipsprogramrom_1_p3, mips_ram_1_p6
  MEM_WB mem_wb_1 (
    .MemoryResult(mips_ram_1_p6), .AluResult({ex_mem_1_aluresult_2_2, ex_mem_1_aluresult_2}),
    .jalPC(ex_mem_1_jalpc_2), .RegDst(ex_mem_1_regdst_2), .RegisterWriteSrc(ex_mem_1_registerwritesrc_2),
    .RegisterWrite(ex_mem_1_registerwrite_2), .Clock(mipsprogramrom_1_p3),
    .MemoryResult_2(mem_wb_1_memoryresult_2), .AluResult_2(mem_wb_1_aluresult_2), .jalPC_2(mem_wb_1_jalpc_2),
    .RegDst_2(registerfile_1_p3), .RegisterWriteSrc_2(mem_wb_1_registerwritesrc_2),
    .RegisterWrite_2(registerfile_1_p2));
  Multiplexer #(.select(2), .width(32)) multiplexer_7 (
    .in0(mem_wb_1_aluresult_2), .in1(mem_wb_1_memoryresult_2), .in2(mem_wb_1_jalpc_2),
    .out(registerfile_1_p1), .sel(mem_wb_1_registerwritesrc_2));  // open: in3

  // Notes on the sheet:
  //   contents of mipsprogramrom_1 (hex, n*v repeats v):
  //   addiu $1, $1, 0x1      # $1 = 0x0001     addiu $2, $2, 0x2      # $2 = 0x0002     slt $3, $1, $2
  //   # $3 = 1     slt $3, $2, $1         # $3 = 0     slti $3, $1, 0x1       # $3 = 1     slti $3, $1,
  //   0x42      # $3 = 0     or $3, $1, $2          # $3 = 0x3     and $3, $1, $2         # $3 = 0     ori
  //   $3, $1, 0x7        # $3 = 0x7     andi $3, $1, 0x7       # $3 = 0x1     sw $3, 0($0)     lw $5,
  //   0($0)     beq $1, $3, LOL     addu $7, $7, $7     addu $7, $7, $7     addu $7, $7, $7     addu $7,
  //   $7, $7     addu $7, $7, $7     addu $7, $7, $7     addu $7, $7, $7
endmodule

module Control (
  input  [5:0] Funct,
  input  [5:0] OP,
  output SignedIMM,
  output [2:0] Alu,
  output [2:0] Branching,
  output [1:0] Memory,
  output [1:0] RegisterWriteSrc,
  output [1:0] RegisterWrite
);

  PLA #(.in_width(6), .truth_table("001000,10#jr\n001001,11#jral")) jr_jral ();  // open: in, out
  PLA #(.in_width(8), .out_width(13), .truth_table("00000000,1100000001010#R-format\n000100xx,0000001000111#beq\n000101xx,0000001010111#bne\n001001xx,1000000001101#addiu\n001010xx,1000000001101#slti\n001100xx,1000000001100#andi\n001101xx,1000000001100#ori\n100011xx,1001010000001#lw\n101011xx,0000100000001#sw\n000010xx,0000001100000#j\n000011xx,1010001100000#jal\n00000010,0000001110000#jr\n00000011,1010001110000#jral")) pla_1 (.out(Memory));  // open: in
endmodule

module Forwarding_unit (
  input  EX_Mem_RegWrite,
  input  [4:0] ID_EX_RegisterRs,
  input  [4:0] ID_EX_RegisterRt,
  input  [4:0] EX_Mem_RegisterRd,
  input  [4:0] EX_Mem_RegisterRt,
  input  Mem_WB_RegWrite,
  input  [4:0] Mem_WB_RegisterRd,
  output [1:0] ForwardA,
  output [1:0] ForwardB
);

  wire and_1_out, and_2_out, comparator_1_eq, comparator_2_eq, comparator_3_eq, comparator_4_eq,
       comparator_5_eq, comparator_6_eq, comparator_7_eq, comparator_8_eq;

  Comparator #(.width(5), .mode("unsigned")) comparator_1 (
    .a(ID_EX_RegisterRs), .b(EX_Mem_RegisterRd), .eq(comparator_1_eq));  // open: gt, lt
  Comparator #(.width(5), .mode("unsigned")) comparator_2 (
    .a(EX_Mem_RegisterRd), .b({5{1'b0}}), .eq(comparator_2_eq));  // open: gt, lt
  Comparator #(.width(5), .mode("unsigned")) comparator_3 (
    .a(EX_Mem_RegisterRd), .b({5{1'b0}}), .eq(comparator_3_eq));  // open: gt, lt
  Comparator #(.width(5), .mode("unsigned")) comparator_4 (
    .a(ID_EX_RegisterRt), .b(EX_Mem_RegisterRt), .eq(comparator_4_eq));  // open: gt, lt
  Comparator #(.width(5), .mode("unsigned")) comparator_5 (
    .a(Mem_WB_RegisterRd), .b({5{1'b0}}), .eq(comparator_5_eq));  // open: gt, lt
  Comparator #(.width(5), .mode("unsigned")) comparator_6 (
    .a(ID_EX_RegisterRs), .b(Mem_WB_RegisterRd), .eq(comparator_6_eq));  // open: gt, lt
  Comparator #(.width(5), .mode("unsigned")) comparator_7 (
    .a(Mem_WB_RegisterRd), .b(ID_EX_RegisterRt), .eq(comparator_7_eq));  // open: gt, lt
  Comparator #(.width(5), .mode("unsigned")) comparator_8 (
    .a(EX_Mem_RegisterRd), .b(ID_EX_RegisterRt), .eq(comparator_8_eq));  // open: gt, lt
  and and_1 (and_1_out, EX_Mem_RegWrite, ~comparator_3_eq, ~comparator_6_eq);  // AND_Gate
  and and_2 (and_2_out, EX_Mem_RegWrite, ~comparator_3_eq, ~comparator_8_eq);  // AND_Gate
  and and_3 (ForwardA[1], EX_Mem_RegWrite, comparator_1_eq, ~comparator_2_eq);  // AND_Gate
  and and_4 (ForwardB[0], EX_Mem_RegWrite, comparator_3_eq, ~comparator_4_eq);  // AND_Gate
  and and_5 (ForwardA[0], Mem_WB_RegWrite, ~comparator_5_eq, ~and_1_out, comparator_6_eq);  // AND_Gate
  and and_6 (ForwardB[1], Mem_WB_RegWrite, ~comparator_5_eq, ~and_2_out, comparator_7_eq);  // AND_Gate
endmodule

module Hazard_detection_unit (
  input  ID_EX_MemRead,
  input  [4:0] ID_EX_RegisterRt,
  input  [4:0] IF_ID_RegisterRs,
  input  [4:0] IF_ID_RegisterRt,
  output STALL
);

  wire comparator_1_eq, comparator_2_eq, or_1_out;

  Comparator #(.width(5), .mode("unsigned")) comparator_1 (
    .a(ID_EX_RegisterRt), .b(IF_ID_RegisterRs), .eq(comparator_1_eq));  // open: gt, lt
  Comparator #(.width(5), .mode("unsigned")) comparator_2 (
    .a(ID_EX_RegisterRt), .b(IF_ID_RegisterRt), .eq(comparator_2_eq));  // open: gt, lt
  or or_1 (or_1_out, comparator_1_eq, comparator_2_eq);
  and and_1 (STALL, ID_EX_MemRead, or_1_out);
endmodule

module ID_EX (
  input  [31:0] Data1,
  input  [31:0] Data2,
  input  [4:0] RegisterRt,
  input  [4:0] RegisterRs,
  input  [31:0] IMM,
  input  [31:0] PC,
  input  [31:0] OP,
  input  [2:0] ALU,
  input  [2:0] Branch,
  input  [1:0] Memory,
  input  [1:0] RegisterWriteSrc,
  input  [1:0] RegisterWrite,
  input  Clear,
  input  Stall,
  input  Clock,
  output [31:0] Data1_2,
  output [31:0] Data2_2,
  output [4:0] RegisterRt_2,
  output [4:0] RegisterRs_2,
  output [31:0] IMM_2,
  output [31:0] PC_2,
  output [31:0] OP_2,
  output [2:0] ALU_2,
  output [2:0] Branch_2,
  output [1:0] Memory_2,
  output [1:0] RegisterWriteSrc_2,
  output [1:0] RegisterWrite_2
);

  wire or_1_out;
  wire [1:0] multiplexer_2_out, multiplexer_3_out;
  wire [2:0] multiplexer_1_out;

  Multiplexer #(.width(3)) multiplexer_1 (.in0(Branch), .in1(3'b000), .out(multiplexer_1_out), .sel(Clear));
  Multiplexer #(.width(2)) multiplexer_2 (.in0(Memory), .in1(2'b00), .out(multiplexer_2_out), .sel(Clear));
  Multiplexer #(.width(2)) multiplexer_3 (.in0(RegisterWrite), .in1(2'b00), .out(multiplexer_3_out), .sel(Clear));
  or or_1 (or_1_out, Clear, ~Stall);  // OR_Gate
  Register #(.width(32)) u_Data1 (.D(Data1), .en(or_1_out), .Q(Data1_2), .clk(Clock));  // open: clr
  Register #(.width(32)) u_Data2 (.D(Data2), .en(or_1_out), .Q(Data2_2), .clk(Clock));  // open: clr
  Register #(.width(5)) u_RegisterRt (.D(RegisterRt), .en(or_1_out), .Q(RegisterRt_2), .clk(Clock));  // open: clr
  Register #(.width(5)) u_RegisterRs (.D(RegisterRs), .en(or_1_out), .Q(RegisterRs_2), .clk(Clock));  // open: clr
  Register #(.width(32)) u_IMM (.D(IMM), .en(or_1_out), .Q(IMM_2), .clk(Clock));  // open: clr
  Register #(.width(32)) u_PC (.D(PC), .en(or_1_out), .Q(PC_2), .clk(Clock));  // open: clr
  Register #(.width(32)) u_OP (.D(OP), .en(or_1_out), .Q(OP_2), .clk(Clock));  // open: clr
  Register #(.width(3)) u_ALU (.D(ALU), .en(or_1_out), .Q(ALU_2), .clk(Clock));  // open: clr
  Register #(.width(3)) u_Branch (.D(multiplexer_1_out), .en(or_1_out), .Q(Branch_2), .clk(Clock));  // open: clr
  Register #(.width(2)) u_Memory (.D(multiplexer_2_out), .en(or_1_out), .Q(Memory_2), .clk(Clock));  // open: clr
  Register #(.width(2)) u_RegisterWriteSrc (
    .D(RegisterWriteSrc), .en(or_1_out), .Q(RegisterWriteSrc_2), .clk(Clock));  // open: clr
  Register #(.width(2)) u_RegisterWrite (
    .D(multiplexer_3_out), .en(or_1_out), .Q(RegisterWrite_2), .clk(Clock));  // open: clr
endmodule

module EX_MEM (
  input  Zero,
  input  [31:0] AluResult,
  input  [31:0] WriteData,
  input  [31:0] BranchPC,
  input  [31:0] JumpPC,
  input  [31:0] jalPC,
  input  [4:0] RegDst,
  input  [2:0] Branch,
  input  [1:0] Memory,
  input  [1:0] RegisterWriteSrc,
  input  RegisterWrite,
  input  Clear,
  input  Stall,
  input  Clock,
  output Zero_2,
  output [31:0] AluResult_2,
  output [31:0] WriteData_2,
  output [31:0] BranchPC_2,
  output [31:0] JumpPC_2,
  output [31:0] jalPC_2,
  output [4:0] RegDst_2,
  output [2:0] Branch_2,
  output [1:0] Memory_2,
  output [1:0] RegisterWriteSrc_2,
  output RegisterWrite_2
);

  wire multiplexer_3_out, or_1_out;
  wire [1:0] multiplexer_2_out;
  wire [2:0] multiplexer_1_out;

  Multiplexer #(.width(3)) multiplexer_1 (.in0(Branch), .in1(3'b000), .out(multiplexer_1_out), .sel(Clear));
  Multiplexer #(.width(2)) multiplexer_2 (.in0(Memory), .in1(2'b00), .out(multiplexer_2_out), .sel(Clear));
  Multiplexer multiplexer_3 (.in0(RegisterWrite), .in1(1'b0), .out(multiplexer_3_out), .sel(Clear));
  or or_1 (or_1_out, Clear, ~Stall);  // OR_Gate
  Register #(.width(1)) u_Zero (.D(Zero), .en(or_1_out), .Q(Zero_2), .clk(Clock));  // open: clr
  Register #(.width(32)) u_AluResult (.D(AluResult), .en(or_1_out), .Q(AluResult_2), .clk(Clock));  // open: clr
  Register #(.width(32)) u_WriteData (.D(WriteData), .en(or_1_out), .Q(WriteData_2), .clk(Clock));  // open: clr
  Register #(.width(32)) u_BranchPC (.D(BranchPC), .en(or_1_out), .Q(BranchPC_2), .clk(Clock));  // open: clr
  Register #(.width(32)) u_JumpPC (.D(JumpPC), .en(or_1_out), .Q(JumpPC_2), .clk(Clock));  // open: clr
  Register #(.width(32)) u_jalPC (.D(jalPC), .en(or_1_out), .Q(jalPC_2), .clk(Clock));  // open: clr
  Register #(.width(5)) u_RegDst (.D(RegDst), .en(or_1_out), .Q(RegDst_2), .clk(Clock));  // open: clr
  Register #(.width(3)) u_Branch (.D(multiplexer_1_out), .en(or_1_out), .Q(Branch_2), .clk(Clock));  // open: clr
  Register #(.width(2)) u_Memory (.D(multiplexer_2_out), .en(or_1_out), .Q(Memory_2), .clk(Clock));  // open: clr
  Register #(.width(2)) u_RegisterWriteSrc (
    .D(RegisterWriteSrc), .en(or_1_out), .Q(RegisterWriteSrc_2), .clk(Clock));  // open: clr
  Register #(.width(1)) u_RegisterWrite (
    .D(multiplexer_3_out), .en(or_1_out), .Q(RegisterWrite_2), .clk(Clock));  // open: clr
endmodule

module MEM_WB (
  input  [31:0] MemoryResult,
  input  [31:0] AluResult,
  input  [31:0] jalPC,
  input  [4:0] RegDst,
  input  [1:0] RegisterWriteSrc,
  input  RegisterWrite,
  input  Clock,
  output [31:0] MemoryResult_2,
  output [31:0] AluResult_2,
  output [31:0] jalPC_2,
  output [4:0] RegDst_2,
  output [1:0] RegisterWriteSrc_2,
  output RegisterWrite_2
);

  Register #(.width(32)) u_MemoryResult (.D(MemoryResult), .en(1'b1), .Q(MemoryResult_2), .clk(Clock));  // open: clr
  Register #(.width(32)) u_AluResult (.D(AluResult), .en(1'b1), .Q(AluResult_2), .clk(Clock));  // open: clr
  Register #(.width(32)) u_jalPC (.D(jalPC), .en(1'b1), .Q(jalPC_2), .clk(Clock));  // open: clr
  Register #(.width(5)) u_RegDst (.D(RegDst), .en(1'b1), .Q(RegDst_2), .clk(Clock));  // open: clr
  Register #(.width(2)) u_RegisterWriteSrc (
    .D(RegisterWriteSrc), .en(1'b1), .Q(RegisterWriteSrc_2), .clk(Clock));  // open: clr
  Register #(.width(1)) u_RegisterWrite (.D(RegisterWrite), .en(1'b1), .Q(RegisterWrite_2), .clk(Clock));  // open: clr
endmodule

module IF_ID (
  input  [31:0] PC,
  input  [31:0] OP,
  input  Clear,
  input  Stall,
  input  Clock,
  output [31:0] PC_2,
  output [31:0] OP_2
);

  wire or_1_out;
  wire [31:0] multiplexer_1_out;

  Multiplexer #(.width(32)) multiplexer_1 (.in0(OP), .in1({32{1'b0}}), .out(multiplexer_1_out), .sel(Clear));
  or or_1 (or_1_out, Clear, ~Stall);  // OR_Gate
  Register #(.width(32)) u_PC (.D(PC), .en(1'b1), .Q(PC_2), .clk(Clock));  // open: clr
  Register #(.width(32)) u_OP (.D(multiplexer_1_out), .en(or_1_out), .Q(OP_2), .clk(Clock));  // open: clr
endmodule

module ALU_Control_2 (
  input  [1:0] ALUop,
  input  [5:0] Funct,
  input  [2:0] IMM_OP,
  output [3:0] Output
);

  PLA #(.in_width(11), .out_width(4), .truth_table("00xxxxxxxxx,0010#lw/sw\n01xxxxxxxxx,0110#beq/bne\n10xxx100001,0010#addu\n10xxx100011,0110#subu\n10xxx100100,0000#AND\n10xxx100101,0001#OR\n10xxx100111,1100#nor\n10xxx101010,0111#slt\n11001xxxxxx,0010#addiu\n11010xxxxxx,0111#slti\n11100xxxxxx,0000#andi\n11101xxxxxx,0001#ori\n10xxx000010,0010#jr\n10xxx000011,0010#jral")) pla_1 (.out(Output));  // open: in
endmodule
